# Fritzing sketch board_controller (saved by Fritzing 0.8.5b)
perfboards: 1

parts:
  U1 = atmega328 [package=dip]  # not connected
  U2 = Voltage Regulator - 5V [package="TO220 [THT]"]  # not connected
  S1 = Pushbutton [package="[THT]"]
  C1 = Capacitor [package=cap-pth-small2]  # not connected
  XTAL1 = Crystal [frequency="16 Mhz" package=THT]  # not connected
  C2 = Capacitor [package=cap-pth-small2]  # not connected
  R2 = Resistor [tolerance=±5% resistance=10k package=THT]  # not connected
  C3 = Electrolytic Capacitor [capacitance=10µF package="100 mil [THT, electrolytic]"]  # not connected
  C4 = Electrolytic Capacitor [capacitance=10µF package="100 mil [THT, electrolytic]"]  # not connected

nets:
  N1: S1.Pin_1, S1.Pin_2
  N2: S1.Pin_3, S1.Pin_4
