# Fritzing sketch board_registers (saved by Fritzing 0.8.5b)
perfboards: 1

parts:
  U1 = 74HC595 [package="DIP16 [THT]"]
  U2 = 74HC595 [package="DIP16 [THT]"]
  R1 = Resistor [tolerance=±5% resistance=22k package=THT]  # not connected
  R2 = Resistor [tolerance=±5% resistance=22k package=THT]  # not connected
  R3 = Resistor [tolerance=±5% resistance=22k package=THT]  # not connected
  R4 = Resistor [tolerance=±5% resistance=22k package=THT]  # not connected
  Q1 = NPN-Transistor [package="TO92 [THT]"]  # not connected
  Q5 = NPN-Transistor [package="TO92 [THT]"]  # not connected
  Q6 = NPN-Transistor [package="TO92 [THT]"]  # not connected
  Q7 = NPN-Transistor [package="TO92 [THT]"]  # not connected
  R5 = Resistor [tolerance=±5% resistance=470 package=THT]  # not connected
  R6 = Resistor [tolerance=±5% resistance=470 package=THT]  # not connected
  R7 = Resistor [tolerance=±5% resistance=470 package=THT]  # not connected
  R8 = Resistor [tolerance=±5% resistance=470 package=THT]  # not connected
  R9 = Resistor [tolerance=±5% resistance=470 package=THT]  # not connected
  R10 = Resistor [tolerance=±5% resistance=470 package=THT]  # not connected
  R11 = Resistor [tolerance=±5% resistance=470 package=THT]  # not connected
  R12 = Resistor [tolerance=±5% resistance=470 package=THT]  # not connected
  R13 = Resistor [tolerance=±5% resistance=470 package=THT]  # not connected

nets:
  N1: U1.Q7', U2.DS
