# Fritzing sketch clock_timer_r1 (saved by Fritzing 0.8.5b)
breadboards: 2

parts:
  S1 = Pushbutton [package="[THT]"]
  S2 = Pushbutton [package="[THT]"]
  S3 = Pushbutton [package="[THT]"]
  R1 = Resistor [tolerance=±5% resistance=10k package=THT]
  IC1 = IC, DIP package, 14 pins [chip_label=74LS14]
  R4 = Resistor [tolerance=±5% resistance=1k package=THT]
  R5 = Resistor [tolerance=±5% resistance=1k package=THT]
  R6 = Resistor [tolerance=±5% resistance=1k package=THT]
  C1 = Electrolytic Capacitor [capacitance=10µF package="100 mil [THT, electrolytic]"]
  C2 = Electrolytic Capacitor [capacitance=10µF package="100 mil [THT, electrolytic]"]
  C3 = Electrolytic Capacitor [capacitance=10µF package="100 mil [THT, electrolytic]"]
  U1 = 74HC595 [package="DIP16 [THT]"]
  U2 = 74HC595 [package="DIP16 [THT]"]
  Q1 = NPN-Transistor [package="TO92 [THT]"]
  Q2 = NPN-Transistor [package="TO92 [THT]"]
  Q3 = NPN-Transistor [package="TO92 [THT]"]
  Q4 = NPN-Transistor [package="TO92 [THT]"]
  R7 = Resistor [tolerance=±5% resistance=22k package=THT]  # not connected
  R8 = Resistor [tolerance=±5% resistance=22k package=THT]
  R9 = Resistor [tolerance=±5% resistance=22k package=THT]
  R10 = Resistor [tolerance=±5% resistance=22k package=THT]
  LED1 = 7-SEGMENT-4DIGIT-YOUNGSUN [package=7-segment-4digit-youngsun]
  R11 = Resistor [tolerance=±5% resistance=470 package=THT]
  R12 = Resistor [tolerance=±5% resistance=470 package=THT]
  R13 = Resistor [tolerance=±5% resistance=470 package=THT]
  R14 = Resistor [tolerance=±5% resistance=470 package=THT]
  R15 = Resistor [tolerance=±5% resistance=470 package=THT]
  R16 = Resistor [tolerance=±5% resistance=470 package=THT]
  R17 = Resistor [tolerance=±5% resistance=470 package=THT]
  R18 = Resistor [tolerance=±5% resistance=470 package=THT]
  R19 = Resistor [tolerance=±5% resistance=470 package=THT]
  Part1 = Arduino Uno (Rev3)
  R20 = Resistor [tolerance=±5% resistance=10k package=THT]
  R21 = Resistor [tolerance=±5% resistance=10k package=THT]
  R22 = Resistor [tolerance=±5% resistance=330 package=THT]
  R23 = Resistor [tolerance=±5% resistance=330 package=THT]
  R24 = Resistor [tolerance=±5% resistance=330 package=THT]
  LED3 = LED - 5mm [color="Red (633nm)" package="5 mm [THT]"]
  LED4 = LED - 5mm [color="Red (633nm)" package="5 mm [THT]"]
  LED5 = LED - 5mm [color="Blue (470nm)" package="5 mm [THT]"]
  J1 = Piezo Speaker
  Q5 = NPN-Transistor [package="TO92 [THT]"]
  R25 = Resistor [tolerance=±5% resistance=22k package=THT]

nets:
  GND: S1.Pin_1, S1.Pin_2, S2.Pin_1, S2.Pin_2, S3.Pin_1, S3.Pin_2, IC1.pin7, C1.-, C2.-, C3.-, U1.GND, U1.OE, U2.GND, U2.OE, Q1.E, Q2.E, Q3.E, Q4.E, LED1.DP, Part1.GND, LED3.cathode, LED4.cathode, LED5.cathode, Q5.E
  N1: S1.Pin_3, S1.Pin_4, R1.Pin_1, R4.Pin_1
  N2: S2.Pin_3, S2.Pin_4, R5.Pin_1, R20.Pin_1
  N3: S3.Pin_3, S3.Pin_4, R6.Pin_1, R21.Pin_1
  VCC: R1.Pin_0, IC1.pin14, U1.MR, U1.VCC, U2.MR, U2.VCC, Part1.5V, R20.Pin_0, R21.Pin_0
  N4: IC1.pin8, Part1.D5_PWM
  N5: IC1.pin9, R6.Pin_0, C3.+
  N6: IC1.pin10, Part1.D6_PWM
  N7: IC1.pin11, R5.Pin_0, C2.+
  N8: IC1.pin12, Part1.D7
  N9: IC1.pin13, R4.Pin_0, C1.+
  N10: U1.Q1, R17.Pin_1
  N11: U1.Q2, R16.Pin_1
  N12: U1.Q3, R15.Pin_1
  N13: U1.Q4, R14.Pin_1
  N14: U1.Q5, R13.Pin_1
  N15: U1.Q6, R12.Pin_1
  N16: U1.Q7, R11.Pin_1
  N17: U1.Q7', U2.DS
  N18: U1.SH_CP, U2.SH_CP, Part1.D2
  N19: U1.ST_CP, U2.ST_CP, Part1.D3_PWM
  N20: U1.DS, Part1.D4
  N21: U1.Q0, R18.Pin_1
  N22: U2.Q2, R8.Pin_0
  N23: U2.Q3, R9.Pin_0
  N24: U2.Q4, R10.Pin_0
  N25: U2.Q0, R19.Pin_1
  N26: Q1.C, LED1.B
  N27: Q2.C, LED1.C
  N28: Q3.C, LED1.COL-C
  N29: Q4.C, LED1.DIG3
  N30: LED1.DIG1, R14.Pin_0
  N31: LED1.DIG2, R15.Pin_0
  N32: LED1.D, R11.Pin_0
  N33: LED1.COL-A, R16.Pin_0
  N34: LED1.E, R12.Pin_0
  N35: LED1.APOS-A, R19.Pin_0
  N36: LED1.F, R17.Pin_0
  N37: LED1.A, R13.Pin_0
  N38: LED1.G, R18.Pin_0
  N39: Part1.D8, R25.Pin_1
  N40: Part1.D9_PWM, R24.Pin_1
  N41: Part1.D10_PWM/SS, R23.Pin_1
  N42: Part1.D11_PWM/MOSI, R22.Pin_1
  N43: Part1.D12/MISO, J1.pin2
  N44: R22.Pin_0, LED5.anode
  N45: R23.Pin_0, LED3.anode
  N46: R24.Pin_0, LED4.anode
  N47: J1.pin1, Q5.C
  N48: Q5.B, R25.Pin_0
